# Fritzing sketch scratch_For_Arduino (saved by Fritzing 0.9.3b)
breadboards: 1

parts:
  R1 = Resistor [tolerance=±5% resistance=220 package=THT]
  LED1 = LED - 5mm [color="Blue (470nm)" package="5 mm [THT]"]
  Part1 = Arduino Uno (Rev3) - ICSP
  LED2 = LED - 5mm [color="Red (633nm)" package="5 mm [THT]"]
  S1 = Pushbutton [package="[SMD]"]
  R2 = Resistor [tolerance=±5% resistance=10k package=THT]
  LDR = Photocell (LDR) [package=THT]
  R4 = Resistor [tolerance=±5% resistance=10k package=THT]
  LM35 = LM35 Temperature Sensor [package="TO92 [THT]"]
  HC-SR501 = HC-SR501 Body Sensor Module

nets:
  N1: R1.Pin_0, LED1.cathode
  GND: R1.Pin_1, R2.Pin_1, R4.Pin_1, LM35.GND, HC-SR501.GND
  N2: LED1.anode, Part1.D9_PWM
  N3: Part1.A0, LDR.pin_1, R4.Pin_0
  N4: Part1.A1, LM35.Vout
  N5: Part1.GND, LED2.cathode
  N6: Part1.D13/SCK, LED2.anode
  N7: Part1.D2, S1.Pin_1, S1.Pin_2, R2.Pin_0
  N8: Part1.D3_PWM, HC-SR501.OUT
  5V: Part1.5V, S1.Pin_3, S1.Pin_4, LDR.pin_0, LM35.+Vs, HC-SR501.VCC

notes:
  D13
  D9
  220 ohm
  10K ohm
  D2
  A0
  A1
  D3

custom parts:
  HC-SR501 Body Sensor Module: Pyroelectric Infrared PIR Motion Sensor Detector Module
